# Fritzing sketch Sketch Fritzing v1 (saved by Fritzing 0.9.3b)
breadboards: 1

parts:
  M1 = >Wemos D1 R32
  DS1 = DS18B20 1-Wire Temperature Sensor Probe Cable
  S1 = PH meter [package=THT]  # not connected
  S2 = Round Pushbutton
  S4 = Round Pushbutton
  KY-1 = Keyes Relay [package=THT]
  L1 = Solenoid
  U1 = LCD-16X2 [package=lcd-16x2_noholes]
  LCM1602_IIC1 = LCM1602 IIC [part_number="LCM1602 IIC" chip_label="LCM1602 IIC" package="DIP (Dual Inline) [THT]"]
  LED1 = RGB LED (com. cathode, rbg) [package="5 mm [THT]"]

nets:
  5V: M1.5V, DS1.VDD
  GND: M1.GND, DS1.GND, S2.leg0, LED1.blue_anode
  N1: M1.IO25, LED1.green_anode
  N2: M1.IO17, LED1.common_cathode
  N3: M1.IO16, LED1.red_anode
  N4: M1.IO14, DS1.shield
  N5: M1.IO13, KY-1.signal
  N6: M1.IO5, S4.leg1
  N7: M1.IO23, S2.leg1
  N8: M1.SDA, LCM1602_IIC1.SDA
  N9: M1.SCL, LCM1602_IIC1.SCL
  N10: KY-1.power, LCM1602_IIC1.VCC
  N11: KY-1.ground, LCM1602_IIC1.GND
  N12: KY-1.C, L1.pin2
  VSS: U1.VSS, LCM1602_IIC1.VSS
  VDD: U1.VDD, LCM1602_IIC1.VDD
  N13: U1.VO, LCM1602_IIC1.V0
  N14: U1.RS, LCM1602_IIC1.RS
  N15: U1.R_W, LCM1602_IIC1.RW
  N16: U1.E, LCM1602_IIC1.E
  N17: U1.DB0, LCM1602_IIC1.D0
  N18: U1.DB1, LCM1602_IIC1.D1
  N19: U1.DB2, LCM1602_IIC1.D2
  N20: U1.DB3, LCM1602_IIC1.D3
  N21: U1.DB4, LCM1602_IIC1.D4
  N22: U1.DB5, LCM1602_IIC1.D5
  N23: U1.DB6, LCM1602_IIC1.D6
  N24: U1.DB7, LCM1602_IIC1.D7
  N25: U1.A, LCM1602_IIC1.A
  N26: U1.K, LCM1602_IIC1.K

notes:
  TDS Meter
  Water Switch Atas
  Water Switch Bawah
  Power AC 220

custom parts:
  >Wemos D1 R32: Wemos D1 R32 - This board is used with dual-mode Wi-Fi and Bluetooth chips, which is safe, reliable, and scalable to a variety of applications. DC in 5V-12V, 1 analog input(3.2V max input), a Micro USB connection, Compatible with D1 R32=WiFi+bluetooth+UNO
  Keyes Relay: The Keyes 5V relay module is suitable for SCM development, home appliance control. It uses a 5V~12V TIL control signal which can control DC / AC signal.
  LCM1602 IIC: I2C-Module to use a 1602 or 2004 LCD on with the wire.h libory Serial LCD Modul
